# Fritzing sketch diagrama-esquematico-capacimetro-portaSerial (saved by Fritzing 0.9.2b)

parts:
  Componente1 = Arduino Uno (Rev3)
  R1 = Resistor [tolerance=±5% resistance=3.3k package="0603 [SMD]"]
  C1 = Ceramic Capacitor [capacitance="100 nF" package="0603 [SMD, multilayer]"]

nets:
  N1: Componente1.A0, R1.Pin_1, C1.0
  N2: Componente1.D2, R1.Pin_0
  N3: Componente1.GND, C1.1

notes:
  3k3
  Capacitor sob teste
